// Logisim project esquematicolab1.circ as structural Verilog: 1 circuit, main circuit main
module main (
  input  A,
  input  B,
  input  C,
  input  D
);

  wire and_1_out, and_2_out, and_3_out, and_4_out, and_5_out, not_1_out, not_2_out, not_3_out, not_4_out,
       not_5_out, not_7_out, or_1_out, or_2_out, or_4_out, or_5_out, or_6_out;

  not not_1 (not_1_out, C);
  not not_2 (not_2_out, D);
  not not_3 (not_3_out, B);
  not not_4 (not_4_out, C);
  not not_5 (not_5_out, D);
  or or_1 (or_1_out, A, B);
  // NOT_Gate not_6 has open pins: in=C, out=open
  not not_7 (not_7_out, D);
  or or_2 (or_2_out, not_3_out, D);
  and and_1 (and_1_out, B, C);
  and and_2 (and_2_out, not_1_out, D);
  and and_3 (and_3_out, not_2_out, C);
  // OR_Gate or_3 has open pins: in0=C, in1=D, out=open
  and and_4 (and_4_out, or_2_out, not_4_out);
  and and_5 (and_5_out, and_1_out, not_5_out);
  or or_4 (or_4_out, and_2_out, and_3_out);
  or or_5 (or_5_out, or_1_out, or_4_out);
  LED led_1 (.in(or_5_out));
  LED led_2 (.in(or_6_out));
  or or_6 (or_6_out, and_4_out, and_5_out);

  // Notes on the sheet:
  //   B
  //   C
  //   D
  //   A
  //   B
  //   C
  //   D
  //   Lógica Bit 0
  //   Lógica Bit 1
endmodule
