// Logisim project simulacaolab1logica.circ as structural Verilog: 1 circuit, main circuit main
module main (
  input  A,
  input  B,
  input  C,
  input  D
);

  wire and_1_out, and_2_out, and_3_out, and_4_out, and_5_out, and_6_out, and_7_out, and_8_out, and_9_out,
       and_10_out, and_11_out, and_12_out, and_13_out, and_14_out, and_15_out, and_16_out, and_17_out,
       nCandD_out, or_1_out, or_2_out, or_3_out, or_4_out, or_5_out, or_6_out, or_7_out;

  and and_1 (and_1_out, ~C, D);  // AND_Gate
  and and_2 (and_2_out, C, ~D);  // AND_Gate
  and and_3 (and_3_out, B, D);
  and and_4 (and_4_out, ~A, ~B, ~C);  // AND_Gate
  and and_5 (and_5_out, B, ~C, D);  // AND_Gate
  and and_6 (and_6_out, B, C, ~D);  // AND_Gate
  and and_7 (and_7_out, ~B, ~C, ~D);  // AND_Gate
  and and_8 (and_8_out, ~C, B, D);  // AND_Gate
  and nCandD (nCandD_out, ~C, D);  // AND_Gate
  and and_9 (and_9_out, ~B, ~C);  // AND_Gate
  and and_10 (and_10_out, B, C, ~D);  // AND_Gate
  and and_11 (and_11_out, ~C, D);  // AND_Gate
  and and_12 (and_12_out, C, ~D);  // AND_Gate
  and and_13 (and_13_out, C, ~D);  // AND_Gate
  and and_14 (and_14_out, B, C);
  and and_15 (and_15_out, B, ~D);  // AND_Gate
  and and_16 (and_16_out, ~C, D);  // AND_Gate
  and and_17 (and_17_out, C, D);
  or or_1 (or_1_out, nCandD_out, and_9_out, and_10_out);
  or or_2 (or_2_out, A, B, and_11_out, and_12_out);
  or or_3 (or_3_out, ~B, and_16_out);  // OR_Gate
  or or_4 (or_4_out, ~B, and_17_out);  // OR_Gate
  or or_5 (or_5_out, and_1_out, and_2_out, and_3_out, and_4_out);
  or or_6 (or_6_out, A, and_5_out, and_6_out, and_7_out, and_8_out);
  or or_7 (or_7_out, A, and_13_out, and_14_out, and_15_out);
  _7_Segment_Display u_7_segment_display_1 (
    .g(or_5_out), .f(or_4_out), .a(or_1_out), .b(or_2_out), .e(or_3_out), .d(or_6_out), .c(or_7_out));  // open: dp

  // Notes on the sheet:
  //   Segmento 6
  //   Segmento 3
  //   Segmento 0
  //   Segmento 1
  //   Segmento 2
  //   Segmento 4
  //   Segmento 5
  //   (Not B) or (Not C and D)
  //   (Not B) or (C and D)
  //   A or (C and Not D) or (B and C) or (B and not D)
endmodule
